// Logisim project fulladder.circ as structural Verilog: 1 circuit, main circuit main
module main (
  input  A4,
  input  A3,
  input  A2,
  input  A1,
  input  B4,
  input  B3,
  input  B2,
  input  B1,
  input  Cin,
  output Cout,
  output S4,
  output S3,
  output S2,
  output S1
);

  wire and_1_out, and_2_out, and_3_out, and_4_out, and_5_out, and_6_out, and_7_out, and_8_out, and_9_out,
       and_10_out, and_11_out, and_12_out, and_13_out, and_14_out, and_15_out, and_16_out, and_17_out,
       and_18_out, and_19_out, and_20_out, and_21_out, and_22_out, and_23_out, and_24_out, and_25_out,
       and_26_out, and_27_out, and_28_out, not_1_out, not_2_out, not_3_out, not_4_out, not_5_out, not_6_out,
       not_7_out, not_8_out, not_9_out, not_10_out, not_11_out, not_12_out, or_2_out, or_4_out, or_6_out;

  not not_1 (not_1_out, A1);
  not not_2 (not_2_out, B1);
  not not_3 (not_3_out, Cin);
  and and_1 (and_1_out, A1, not_3_out, not_2_out);
  and and_2 (and_2_out, Cin, not_2_out, not_1_out);
  and and_3 (and_3_out, B1, not_1_out, not_3_out);
  and and_4 (and_4_out, A1, B1, Cin);
  and and_5 (and_5_out, B1, Cin);
  and and_6 (and_6_out, B1, A1, not_3_out);
  and and_7 (and_7_out, A1, Cin, not_2_out);
  or or_1 (S1, and_1_out, and_2_out, and_3_out, and_4_out);
  or or_2 (or_2_out, and_5_out, and_6_out, and_7_out);
  not not_4 (not_4_out, A2);
  not not_5 (not_5_out, B2);
  not not_6 (not_6_out, or_2_out);
  and and_8 (and_8_out, A2, not_6_out, not_5_out);
  and and_9 (and_9_out, or_2_out, not_5_out, not_4_out);
  and and_10 (and_10_out, B2, not_4_out, not_6_out);
  and and_11 (and_11_out, A2, B2, or_2_out);
  and and_12 (and_12_out, B2, or_2_out);
  and and_13 (and_13_out, B2, A2, not_6_out);
  and and_14 (and_14_out, A2, or_2_out, not_5_out);
  or or_3 (S2, and_8_out, and_9_out, and_10_out, and_11_out);
  or or_4 (or_4_out, and_12_out, and_13_out, and_14_out);
  not not_7 (not_7_out, A3);
  not not_8 (not_8_out, B3);
  not not_9 (not_9_out, or_4_out);
  and and_15 (and_15_out, A3, not_9_out, not_8_out);
  and and_16 (and_16_out, or_4_out, not_8_out, not_7_out);
  and and_17 (and_17_out, B3, not_7_out, not_9_out);
  and and_18 (and_18_out, A3, B3, or_4_out);
  and and_19 (and_19_out, B3, or_4_out);
  and and_20 (and_20_out, B3, A3, not_9_out);
  and and_21 (and_21_out, A3, or_4_out, not_8_out);
  or or_5 (S3, and_15_out, and_16_out, and_17_out, and_18_out);
  or or_6 (or_6_out, and_19_out, and_20_out, and_21_out);
  not not_10 (not_10_out, A4);
  not not_11 (not_11_out, B4);
  not not_12 (not_12_out, or_6_out);
  and and_22 (and_22_out, A4, not_12_out, not_11_out);
  and and_23 (and_23_out, or_6_out, not_11_out, not_10_out);
  and and_24 (and_24_out, B4, not_10_out, not_12_out);
  and and_25 (and_25_out, A4, B4, or_6_out);
  and and_26 (and_26_out, B4, or_6_out);
  and and_27 (and_27_out, B4, A4, not_12_out);
  and and_28 (and_28_out, A4, or_6_out, not_11_out);
  or or_7 (Cout, and_26_out, and_27_out, and_28_out);
  or or_8 (S4, and_22_out, and_23_out, and_24_out, and_25_out);
endmodule
